// Logisim project milestone 1 .circ as structural Verilog: 1 circuit, main circuit main
module main (
  input  [7:0] in_1,
  input  in_2,
  input  Load,
  input  Store,
  input  [2:0] in_5,
  input  Load_2,
  input  in_7,
  input  Load_3,
  input  in_9,
  input  in_10,
  input  Load_4,
  input  in_12,
  input  in_13,
  input  in_14,
  input  Load_5,
  input  in_16,
  input  in_17
);

  wire Clock_out;
  wire [3:0] AR_q, bitselector_1_out;
  wire [7:0] AC_q, adder_1_out, bit_extender_1_out, DR_q, multiplexer_1_out, multiplexer_2_out, ram_1_data,
       subtractor_1_out, TR_q;

  Clock Clock (.out(Clock_out));
  Register AC (.D(multiplexer_2_out), .en(Load_2), .Q(AC_q), .clk(Clock_out), .clr(in_7));
  Register DR (.D(multiplexer_1_out), .en(Load_3), .Q(DR_q), .clk(Clock_out), .clr(in_10));
  Register TR (.D(multiplexer_1_out), .en(Load_4), .Q(TR_q), .clk(Clock_out), .clr(in_12));
  BitSelector #(.group(4)) bitselector_1 (.in(multiplexer_1_out), .out(bitselector_1_out));  // open: sel
  Register #(.width(4)) AR (.D(bitselector_1_out), .en(Load_5), .Q(AR_q), .clk(Clock_out), .clr(in_16));
  RAM #(.addrWidth(4), .bus("separate")) ram_1 (
    .addr(AR_q), .din(multiplexer_1_out), .data(ram_1_data), .str(Store), .clk(Clock_out), .ld(Load),
    .clr(in_2));  // open: sel
  assign bit_extender_1_out = {{4{1'b0}}, AR_q};  // Bit_Extender bit_extender_1
  Multiplexer #(.select(3), .width(8), .disabled(0)) multiplexer_1 (
    .in0(ram_1_data), .in1(AC_q), .in2(DR_q), .in3(TR_q), .in4(bit_extender_1_out), .in5(in_1), .in6(in_1),
    .in7(in_1), .out(multiplexer_1_out), .sel(in_5), .en(1'b1));
  Subtractor subtractor_1 (.a(AC_q), .b(DR_q), .out(subtractor_1_out), .bin(in_9));  // open: bout
  Adder adder_1 (.a(DR_q), .b(AC_q), .out(adder_1_out), .cin(in_13));  // open: cout
  Multiplexer #(.width(8)) multiplexer_2 (
    .in0(adder_1_out), .in1(subtractor_1_out), .out(multiplexer_2_out), .sel(in_17), .en(in_14));
endmodule
